# Fritzing sketch attiny_photoresistor_i2c (saved by Fritzing 0.9.2b)
breadboards: 1

parts:
  ATtiny85 = attiny85 [package=dip]
  R1 = PHOTOCELL [part_number=Photoresistor package=photocell]
  LED1 = LEDs [package=led10mm]
  R2 = Resistor [tolerance=±5% resistance=220 package="2010 [SMD]"]
  R3 = Resistor [tolerance=±5% resistance=10k package="2010 [SMD]"]

nets:
  N1: ATtiny85.Pin_2, R1.P$1, R3.Pin_0
  N2: ATtiny85.Pin_3, LED1.A
  GND: ATtiny85.Pin_4, R2.Pin_1, R3.Pin_1
  SDA: ATtiny85.Pin_5
  SCL: ATtiny85.Pin_7
  +5V: ATtiny85.Pin_8, R1.P$2
  N3: LED1.C, R2.Pin_0
